# Fritzing sketch BT_LEDS (saved by Fritzing 0.9.3b)
breadboards: 1

parts:
  LCD1 = LCD screen
  Part1 = Arduino Mega 2560 (Rev3)
  R1 = Trimmer Potentiometer [maximum_resistance=10kΩ package=THT]
  R2 = Resistor [tolerance=±5% resistance=220 package="1206 [SMD]"]
  BT1 = Bluetooth HC-06u [package=THT]
  LED2 = LED - 3mm [color="Yellow (595nm)" package="3 mm [THT]"]
  LED3 = LED - 3mm [color="Green (555nm)" package="3 mm [THT]"]
  LED4 = LED - 3mm [color="Red (633nm)" package="3 mm [THT]"]
  R3 = Resistor [tolerance=±5% resistance=220 package="1206 [SMD]"]
  R4 = Resistor [tolerance=±5% resistance=220 package="1206 [SMD]"]
  R5 = Resistor [tolerance=±5% resistance=220 package="1206 [SMD]"]

nets:
  GND: LCD1.VSS, LCD1.R/W, LCD1.LED-, Part1.GND, R1.leg2, BT1.GND, LED2.cathode, LED3.cathode, LED4.cathode
  VDD: LCD1.VDD, Part1.5V, R1.leg1, R2.Pin_0, BT1.VCC
  N1: LCD1.V0, R1.wiper
  N2: LCD1.RS, Part1.D12_PWM
  N3: LCD1.E, Part1.D11_PWM
  N4: LCD1.DB4, Part1.D2_PWM
  N5: LCD1.DB5, Part1.D3_PWM
  N6: LCD1.DB6, Part1.D4_PWM
  N7: LCD1.DB7, Part1.D5_PWM
  N8: LCD1.LED+, R2.Pin_1
  N9: Part1.D19/RX1, BT1.TXD
  N10: Part1.D18/TX1, BT1.RXD
  N11: Part1.D10_PWM, LED4.anode, R4.Pin_0, R4.Pin_1
  N12: Part1.D9_PWM, LED2.anode, R5.Pin_0, R5.Pin_1
  N13: Part1.D8_PWM, LED3.anode, R3.Pin_0, R3.Pin_1

custom parts:
  Bluetooth HC-06u: Bluetooth HC-06 - face up, pins down 16.5mm x 37.5mm PCB
